# Fritzing sketch Barco (saved by Fritzing 1.0.2b)

parts:
  Part1 = Arduino Uno (Rev3)
  920KV_Motor1 = DJI 920 KV Motor
  M1 = ESC
  Power_plug2 = Power plug  # not connected
  M2 = ESC
  920KV_Motor2 = DJI 920 KV Motor
  J1 = Basic Servo
  J2 = Basic Servo
  J3 = Basic Servo
  J4 = Basic Servo
  Power_plug3 = Power plug
  Mod1 = Heltec WiFi LoRa 32 V2 [part_number=HTIT-WB32LA]

nets:
  N1: Part1.D9_PWM, M1.DATA
  N2: Part1.D10_PWM/SS, J2.pulse
  N3: Part1.D11_PWM/MOSI, J4.pulse
  N4: Part1.D12/MISO, Mod1.pin_35
  N5: Part1.D13/SCK, Mod1.pin_36
  N6: Part1.D3_PWM, M2.DATA
  N7: Part1.D5_PWM, J1.pulse
  N8: Part1.D6_PWM, J3.pulse
  GND: Part1.GND, Power_plug3.GND
  N9: 920KV_Motor1.w, M1.W
  N10: 920KV_Motor1.v, M1.V
  N11: 920KV_Motor1.u, M1.U
  N12: M2.U, 920KV_Motor2.u
  N13: M2.V, 920KV_Motor2.v
  N14: M2.W, 920KV_Motor2.w
  GND_2: J1.gnd, J2.gnd, J3.gnd
  VCC: J1.vcc, J2.vcc, J3.vcc, J4.vcc, Power_plug3.VCC

notes:
  ESC
  UNO
  INPUT Voltage ESC
  7 - 10 V DC
  ADAPTER
  INPUT Voltage Servos
  5 - 7 V DC
  ESP32

custom parts:
  DJI 920 KV Motor: DJI Brushless Outrunner 2212/920K Motor F330-550
