# Fritzing sketch GO_ESP32 (saved by Fritzing 1.0.2b)

parts:
  J2 = Basic Servo
  Power_plug3 = Power plug
  J1 = Basic Servo
  Mod1 = Heltec WiFi LoRa 32 V2 [part_number=HTIT-WB32LA]

nets:
  GND: J2.gnd, Power_plug3.GND, J1.gnd
  VCC: J2.vcc, Power_plug3.VCC, J1.vcc
  N1: J2.pulse, Mod1.pin_9
  N2: J1.pulse, Mod1.pin_8

notes:
  INPUT Voltage Servos
  5 - 7 V DC
  UNO
