# Fritzing sketch GO_UNO (saved by Fritzing 1.0.2b)

parts:
  Componente1 = Arduino Uno (Rev3) - ICSP
  J2 = Basic Servo
  Power_plug3 = Power plug
  J1 = Basic Servo

nets:
  N1: Componente1.D9_PWM, J1.pulse
  N2: Componente1.D10_PWM/SS, J2.pulse
  GND: J2.gnd, Power_plug3.GND, J1.gnd
  VCC: J2.vcc, Power_plug3.VCC, J1.vcc

notes:
  INPUT Voltage Servos
  5 - 7 V DC
  UNO
